// Logisim project controller.circ as structural Verilog: 1 circuit, main circuit main
module main (
);

  wire clock_1_out, dipswitch_1_p1, dipswitch_1_p2, dipswitch_1_p3, dipswitch_1_p4, dipswitch_1_p5,
       dipswitch_1_p6, dipswitch_1_p7, dipswitch_1_p8, multiplexer_1_out;
  wire [4:0] counter_1_q;

  Clock clock_1 (.out(clock_1_out));
  // DipSwitch #(.NSwitches(8)) dipswitch_1: pin names not known; wires that end beside it: dipswitch_1_p1, dipswitch_1_p2, dipswitch_1_p3, dipswitch_1_p4, dipswitch_1_p5, dipswitch_1_p6, dipswitch_1_p7, dipswitch_1_p8
  Counter #(.width(5), .max('h1f)) counter_1 (
    .Q(counter_1_q), .clk(clock_1_out));  // open: load, D, count, carry, clr, preset, down
  Multiplexer #(.select(5), .enable("false")) multiplexer_1 (
    .in0(1'b1), .in1(dipswitch_1_p1), .in2(1'b0), .in3(1'b1), .in4(dipswitch_1_p2), .in5(1'b0), .in6(1'b1),
    .in7(dipswitch_1_p3), .in8(1'b0), .in9(1'b1), .in10(dipswitch_1_p4), .in11(1'b0), .in12(1'b1),
    .in13(dipswitch_1_p5), .in14(1'b0), .in15(1'b1), .in16(dipswitch_1_p6), .in17(1'b0), .in18(1'b1),
    .in19(dipswitch_1_p7), .in20(1'b0), .in21(1'b1), .in22(dipswitch_1_p8), .in23(1'b0), .in24(1'b1),
    .in25(1'b1), .in26(1'b1), .in27(1'b0), .in28(1'b0), .in29(1'b0), .in30(1'b0), .in31(1'b0),
    .out(multiplexer_1_out), .sel(counter_1_q));
  LED led_1 (.in(multiplexer_1_out));
endmodule
